// Logisim project lab2.circ as structural Verilog: 1 circuit, main circuit 四位二进制可逆计数器
module \四位二进制可逆计数器  (
  input  in_1,
  input  in_2,
  input  in_3,
  output out_4,
  output out_5,
  output out_6,
  output out_7
);

  wire and_1_out, and_2_out, and_3_out, and_4_out, and_5_out, and_6_out, clock_1_out, nQA, nQB, nQC, nQD,
       or_1_out, or_2_out, or_3_out;

  Clock clock_1 (.out(clock_1_out));
  D_Flip_Flop A (.clk(clock_1_out), .D(nQA), .Q(out_7), .Qn(nQA), .reset(in_2));  // open: preset, en
  and and_1 (and_1_out, in_1, out_6, out_7);
  and and_2 (and_2_out, in_3, nQB, nQA);
  and and_3 (and_3_out, in_1, out_5, out_6, out_7);
  and and_4 (and_4_out, in_3, nQC, nQB, nQA);
  or or_1 (or_1_out, and_1_out, and_2_out);
  or or_2 (or_2_out, and_3_out, and_4_out);
  and and_5 (and_5_out, in_1, out_7);
  or or_3 (or_3_out, and_5_out, and_6_out);
  and and_6 (and_6_out, in_3, nQA);
  D_Flip_Flop C (.clk(or_1_out), .D(nQC), .Q(out_5), .Qn(nQC), .reset(in_2));  // open: preset, en
  D_Flip_Flop D (.clk(or_2_out), .D(nQD), .Q(out_4), .Qn(nQD), .reset(in_2));  // open: preset, en
  D_Flip_Flop B (.clk(or_3_out), .D(nQB), .Q(out_6), .Qn(nQB), .reset(in_2));  // open: preset, en

  // Other names for the same wires on the sheet: CLR = in_2; CPD = in_3; CPU = in_1; QA = out_7; QB = out_6;
  //   QC = out_5; QD = out_4
endmodule
